# Fritzing sketch Cava (saved by Fritzing 0.9.3b)
breadboards: 1

parts:
  S1 = Momentary Switch [package=ksa_sealed_tac_switch]
  S2 = Momentary Switch [package=ksa_sealed_tac_switch]
  U1 = 7-SEGMENT-DISPLAY [package=7-segment-display]  # not connected
  U2 = 7-SEGMENT-DISPLAY [package=7-segment-display]  # not connected
  U3 = SN74LS47N [package="DIP16 [THT]"]
  U4 = SN74LS47N [package="DIP16 [THT]"]
  Componente1 = Arduino Uno (Rev3)  # not connected
  J1 = Peltier Element
  U5 = TMP102 [package=sot563]
  IC1 = L293D [package=THT]
  R1 = Resistor [tolerance=±5% resistance=4.7k package="1206 [SMD]"]
  R2 = Resistor [tolerance=±5% resistance=4.7k package="1206 [SMD]"]
  C1 = Tantalum Capacitor [capacitance=1μF package="200 mil [THT, tantalum]"]
  C2 = Tantalum Capacitor [capacitance=1μF package="200 mil [THT, tantalum]"]

nets:
  GND: S1.4, S2.4, U3.GND, U4.GND, U5.GND, IC1.0V, C1.-, C2.-
  VCC: U3.VCC, U4.VCC, U5.ADD0, U5.VCC, IC1.+V
  N1: J1.pin1, R1.Pin_0, C1.+
  N2: J1.pin2, R2.Pin_0, C2.+
  N3: IC1.In_1, R1.Pin_1
  N4: IC1.Out_2_(_Controlled_by_Enable_1_), R2.Pin_1

custom parts:
  SN74LS47N: BCD-TO-SEVEN-SEGMENT DECODERS/DRIVRES
